# Fritzing sketch einbahnstrassen (saved by Fritzing 0.9.3b)
breadboards: 1

parts:
  Bauteil1 = Arduino Uno (Rev3)
  SP1 = SPEAKER [package=pcb_mount_speaker]
  C1 = Electrolytic Capacitor [capacitance=10µF package="100 mil [THT, electrolytic]"]
  R1 = Photocell (LDR) [package=THT]
  R2 = Photocell (LDR) [package=THT]
  LED1 = LED - 5mm [color="Red (633nm)" package="5 mm [THT]"]
  LED2 = LED - 5mm [color="Red (633nm)" package="5 mm [THT]"]
  LED3 = LED - 5mm [color="Red (633nm)" package="5 mm [THT]"]
  R3 = Resistor [tolerance=±5% resistance=220 package="2010 [SMD]"]
  R4 = Resistor [tolerance=±5% resistance=220 package="2010 [SMD]"]
  R5 = Resistor [tolerance=±5% resistance=220 package="2010 [SMD]"]
  R6 = Resistor [tolerance=±5% resistance=1k package="2010 [SMD]"]
  R7 = Resistor [tolerance=±5% resistance=1k package="2010 [SMD]"]
  S1 = Round Pushbutton
  R8 = Resistor [tolerance=±5% resistance=1k package="2010 [SMD]"]

nets:
  N1: Bauteil1.A1, R2.pin_0, R6.Pin_0
  N2: Bauteil1.A2, R1.pin_0, R7.Pin_0
  N3: Bauteil1.D8, C1.+
  N4: Bauteil1.GND, SP1.-, LED1.cathode, LED2.cathode, LED3.cathode, R6.Pin_1, R7.Pin_1, R8.Pin_1
  N5: Bauteil1.D2, S1.leg0
  N6: Bauteil1.D3_PWM, R3.Pin_0
  N7: Bauteil1.D4, R4.Pin_0
  N8: Bauteil1.D5_PWM, R5.Pin_0
  N9: Bauteil1.5V, R1.pin_1, R2.pin_1, S1.leg1, R8.Pin_0
  N10: SP1.+, C1.-
  N11: LED1.anode, R3.Pin_1
  N12: LED2.anode, R4.Pin_1
  N13: LED3.anode, R5.Pin_1
